// Logisim project ex2.circ as structural Verilog: 1 circuit, main circuit compute_BrUn
module compute_BrUn (
  input  [31:0] INSTRUCTION,
  output BrUn
);


  assign BrUn = INSTRUCTION[13];
  // also tied to GND on the sheet: {INSTRUCTION[0], INSTRUCTION[1], INSTRUCTION[2], INSTRUCTION[3], INSTRUCTION[4], INSTRUCTION[5], INSTRUCTION[6], INSTRUCTION[7], INSTRUCTION[8], INSTRUCTION[9], INSTRUCTION[10], INSTRUCTION[11], INSTRUCTION[12], INSTRUCTION[14], INSTRUCTION[15], INSTRUCTION[16], INSTRUCTION[17], INSTRUCTION[18], INSTRUCTION[19], INSTRUCTION[20], INSTRUCTION[21], INSTRUCTION[22], INSTRUCTION[23], INSTRUCTION[24], INSTRUCTION[25], INSTRUCTION[26], INSTRUCTION[27], INSTRUCTION[28], INSTRUCTION[29], INSTRUCTION[30], INSTRUCTION[31]}
endmodule
