// Logisim project alu.circ as structural Verilog: 1 circuit, main circuit alu
module alu (
  input  [31:0] A,
  input  [31:0] B,
  input  [3:0] ALUSel,
  output [31:0] ALUResult
);

  wire comparator_1_lt, comparator_2_eq, comparator_3_eq, comparator_4_eq, comparator_5_eq, comparator_6_eq,
       comparator_7_eq, comparator_8_eq, comparator_9_eq, comparator_10_eq, comparator_11_eq,
       comparator_12_eq, comparator_13_eq, comparator_14_eq;
  wire [31:0] add0, and7, mul8, mulh9, mulhu11, or6, result0, result1, result2, result4, result5, result6,
       result7, result8, result9, result11, result12, result13, result15, sll1, slt2, sra13, srl5, sub12,
       xor4;

  Adder #(.width(32)) adder_1 (.a(A), .b(B), .out(add0));  // open: cin, cout
  Shifter #(.width(32)) shifter_1 (.in(A), .\dist (B[4:0]), .out(sll1));
  Comparator #(.width(32)) comparator_1 (.a(A), .b(B), .lt(comparator_1_lt));  // open: gt, eq
  assign xor4 = A ^ B;  // XOR_Gate xor_1, 32 bits wide
  Shifter #(.shift("lr"), .width(32)) shifter_2 (.in(A), .\dist (B[4:0]), .out(srl5));
  assign or6 = A | B;  // OR_Gate or_1, 32 bits wide
  assign and7 = A & B;  // AND_Gate and_1, 32 bits wide
  Multiplier #(.mode("twosComplement"), .width(32)) multiplier_1 (.a(A), .b(B), .out(mul8));  // open: cin, cout
  Multiplier #(.mode("twosComplement"), .width(32)) multiplier_2 (.a(A), .b(B), .cout(mulh9));  // open: out, cin
  Multiplier #(.width(32)) multiplier_3 (.a(A), .b(B), .cout(mulhu11));  // open: out, cin
  Subtractor #(.width(32)) subtractor_1 (.a(A), .b(B), .out(sub12));  // open: bin, bout
  Shifter #(.shift("ar"), .width(32)) shifter_3 (.in(A), .\dist (B[4:0]), .out(sra13));
  Multiplexer #(.width(32)) multiplexer_1 (.in0({32{1'b0}}), .in1(32'h1), .out(slt2), .sel(comparator_1_lt));
  Comparator #(.width(4)) comparator_2 (.a(4'b0101), .b(ALUSel), .eq(comparator_2_eq));  // open: gt, lt
  Comparator #(.width(4)) comparator_3 (.a(4'b0110), .b(ALUSel), .eq(comparator_3_eq));  // open: gt, lt
  Comparator #(.width(4)) comparator_4 (.a(4'b0111), .b(ALUSel), .eq(comparator_4_eq));  // open: gt, lt
  Comparator #(.width(4)) comparator_5 (.a(4'b1000), .b(ALUSel), .eq(comparator_5_eq));  // open: gt, lt
  Comparator #(.width(4)) comparator_6 (.a(4'b1001), .b(ALUSel), .eq(comparator_6_eq));  // open: gt, lt
  Comparator #(.width(4)) comparator_7 (.a(4'b1011), .b(ALUSel), .eq(comparator_7_eq));  // open: gt, lt
  Comparator #(.width(4)) comparator_8 (.a(4'b1100), .b(ALUSel), .eq(comparator_8_eq));  // open: gt, lt
  Comparator #(.width(4)) comparator_9 (.a(4'b1101), .b(ALUSel), .eq(comparator_9_eq));  // open: gt, lt
  Comparator #(.width(4)) comparator_10 (.a(4'b1111), .b(ALUSel), .eq(comparator_10_eq));  // open: gt, lt
  Multiplexer #(.width(32)) multiplexer_2 (.in0({32{1'b0}}), .in1(add0), .out(result0), .sel(comparator_11_eq));
  Comparator #(.width(4)) comparator_11 (.a(4'b0000), .b(ALUSel), .eq(comparator_11_eq));  // open: gt, lt
  Multiplexer #(.width(32)) multiplexer_3 (.in0({32{1'b0}}), .in1(sll1), .out(result1), .sel(comparator_12_eq));
  Comparator #(.width(4)) comparator_12 (.a(4'b0001), .b(ALUSel), .eq(comparator_12_eq));  // open: gt, lt
  Multiplexer #(.width(32)) multiplexer_4 (.in0({32{1'b0}}), .in1(slt2), .out(result2), .sel(comparator_13_eq));
  Comparator #(.width(4)) comparator_13 (.a(4'b0010), .b(ALUSel), .eq(comparator_13_eq));  // open: gt, lt
  Multiplexer #(.width(32)) multiplexer_5 (.in0({32{1'b0}}), .in1(xor4), .out(result4), .sel(comparator_14_eq));
  Comparator #(.width(4)) comparator_14 (.a(4'b0100), .b(ALUSel), .eq(comparator_14_eq));  // open: gt, lt
  Multiplexer #(.width(32)) multiplexer_6 (.in0({32{1'b0}}), .in1(srl5), .out(result5), .sel(comparator_2_eq));
  Multiplexer #(.width(32)) multiplexer_7 (.in0({32{1'b0}}), .in1(or6), .out(result6), .sel(comparator_3_eq));
  Multiplexer #(.width(32)) multiplexer_8 (.in0({32{1'b0}}), .in1(and7), .out(result7), .sel(comparator_4_eq));
  Multiplexer #(.width(32)) multiplexer_9 (.in0({32{1'b0}}), .in1(mul8), .out(result8), .sel(comparator_5_eq));
  Multiplexer #(.width(32)) multiplexer_10 (.in0({32{1'b0}}), .in1(mulh9), .out(result9), .sel(comparator_6_eq));
  Multiplexer #(.width(32)) multiplexer_11 (.in0({32{1'b0}}), .in1(mulhu11), .out(result11), .sel(comparator_7_eq));
  Multiplexer #(.width(32)) multiplexer_12 (.in0({32{1'b0}}), .in1(sub12), .out(result12), .sel(comparator_8_eq));
  Multiplexer #(.width(32)) multiplexer_13 (.in0({32{1'b0}}), .in1(sra13), .out(result13), .sel(comparator_9_eq));
  Multiplexer #(.width(32)) multiplexer_14 (.in0({32{1'b0}}), .in1(B), .out(result15), .sel(comparator_10_eq));
  assign ALUResult = result0 | result1 | result2 | result4 | result5 | result6 | result7 | result8 | result9 | result11 | result12 | result13 | result15;  // OR_Gate or_2, 32 bits wide

  // Other names for the same wires on the sheet: bsel15[31:0] = B

  // Notes on the sheet:
  //   INPUTS to your circuit
  //   DON'T CHANGE THE LOCATIONS OF THE INPUTS AND OUTPUTS!
  //   OUTPUT from your circuit
endmodule
