// Logisim project control-logic.circ as structural Verilog: 1 circuit, main circuit control_logic
module control_logic (
  input  [31:0] Instruction,
  input  BrEq,
  input  BrLt,
  output PCSel,
  output RegWEn,
  output [2:0] ImmSel,
  output BrUn,
  output ASel,
  output BSel,
  output [3:0] ALUSel,
  output MemWEn,
  output [1:0] WBSel
);

  wire and_1_out, and_2_out, and_3_out, and_4_out, and_5_out, and_6_out, and_7_out, and_8_out, and_9_out,
       and_10_out, and_11_out, and_12_out, and_13_out, and_14_out, and_15_out, and_16_out, and_17_out,
       and_18_out, and_19_out, and_20_out, and_21_out, comparator_1_eq, comparator_2_eq, comparator_3_eq,
       comparator_4_eq, comparator_5_eq, comparator_6_eq, comparator_7_eq, comparator_8_eq, comparator_9_eq,
       comparator_10_eq, comparator_11_eq, comparator_12_eq, comparator_13_eq, comparator_14_eq,
       comparator_15_eq, comparator_16_eq, comparator_17_eq, comparator_18_eq, comparator_19_eq,
       comparator_20_eq, comparator_21_eq, comparator_22_eq, comparator_23_eq, comparator_24_eq,
       comparator_25_eq, comparator_26_eq, comparator_27_eq, comparator_28_eq, comparator_29_eq,
       comparator_30_eq, comparator_31_eq, comparator_32_eq, comparator_33_eq, comparator_34_eq,
       comparator_35_eq, comparator_36_eq, comparator_37_eq, comparator_38_eq, not_1_out, not_2_out,
       not_3_out, or_2_out, or_5_out, PCSel1, PCSel2;
  wire [1:0] priority_encoder_1_out, priority_encoder_4_out;
  wire [2:0] priority_encoder_2_out, priority_encoder_5_out;
  wire [3:0] priority_encoder_3_out;
  wire [5:0] adder_1_out, adder_2_out, adder_3_out, adder_4_out, adder_5_out, bit_extender_1_out,
       bit_extender_2_out, bit_extender_3_out, bit_extender_4_out, bit_extender_5_out, bit_extender_6_out,
       or_1_out, ROMInputB, ROMInputI1, ROMInputI2, ROMInputOther, ROMInputR, ROMInputS;
  wire [15:14] rom_1_data;

  Comparator #(.mode("unsigned"), .width(7)) comparator_1 (
    .a(Instruction[6:0]), .b(7'b0010111), .eq(comparator_1_eq));  // open: gt, lt
  Comparator #(.mode("unsigned"), .width(7)) comparator_2 (
    .a(Instruction[6:0]), .b(7'b0110111), .eq(comparator_2_eq));  // open: gt, lt
  Comparator #(.mode("unsigned"), .width(7)) comparator_3 (
    .a(Instruction[6:0]), .b(7'b1101111), .eq(comparator_3_eq));  // open: gt, lt
  Comparator #(.mode("unsigned"), .width(7)) comparator_4 (
    .a(Instruction[6:0]), .b(7'b1100111), .eq(comparator_4_eq));  // open: gt, lt
  ROM #(.addrWidth(6), .dataWidth(16)) rom_1 (
    .addr(or_1_out), .data({rom_1_data, WBSel, MemWEn, ALUSel, BSel, ASel, BrUn, ImmSel, RegWEn}));
  assign or_1_out = ROMInputR | ROMInputI1 | ROMInputI2 | ROMInputS | ROMInputB | ROMInputOther;  // OR_Gate or_1, 6 bits wide
  Priority_Encoder #(.select_enc(2)) priority_encoder_1 (
    .in0(comparator_1_eq), .in1(comparator_2_eq), .in2(comparator_3_eq), .in3(comparator_4_eq),
    .out(priority_encoder_1_out));  // open: gs, en_out, en_in
  assign bit_extender_1_out = {{4{1'b0}}, priority_encoder_1_out};  // Bit_Extender bit_extender_1
  Adder #(.width(6)) adder_1 (.a(bit_extender_1_out), .b(6'b100000), .out(adder_1_out));  // open: cin, cout
  or or_2 (or_2_out, comparator_1_eq, comparator_2_eq, comparator_3_eq, comparator_4_eq);
  or or_3 (PCSel2, comparator_3_eq, comparator_4_eq);
  Multiplexer #(.width(6)) multiplexer_1 (.in0({6{1'b0}}), .in1(adder_1_out), .out(ROMInputOther), .sel(or_2_out));
  or or_4 (PCSel, PCSel1, PCSel2);
  Comparator #(.mode("unsigned"), .width(3)) comparator_5 (
    .a(3'b000), .b(Instruction[14:12]), .eq(comparator_5_eq));  // open: gt, lt
  Comparator #(.mode("unsigned"), .width(3)) comparator_6 (
    .a(3'b001), .b(Instruction[14:12]), .eq(comparator_6_eq));  // open: gt, lt
  Comparator #(.mode("unsigned"), .width(3)) comparator_7 (
    .a(3'b010), .b(Instruction[14:12]), .eq(comparator_7_eq));  // open: gt, lt
  Comparator #(.mode("unsigned"), .width(3)) comparator_8 (
    .a(3'b011), .b(Instruction[14:12]), .eq(comparator_8_eq));  // open: gt, lt
  Comparator #(.mode("unsigned"), .width(3)) comparator_9 (
    .a(3'b100), .b(Instruction[14:12]), .eq(comparator_9_eq));  // open: gt, lt
  Comparator #(.mode("unsigned"), .width(3)) comparator_10 (
    .a(3'b101), .b(Instruction[14:12]), .eq(comparator_10_eq));  // open: gt, lt
  Comparator #(.mode("unsigned"), .width(3)) comparator_11 (
    .a(3'b110), .b(Instruction[14:12]), .eq(comparator_11_eq));  // open: gt, lt
  Comparator #(.mode("unsigned"), .width(3)) comparator_12 (
    .a(3'b111), .b(Instruction[14:12]), .eq(comparator_12_eq));  // open: gt, lt
  Comparator #(.mode("unsigned"), .width(7)) comparator_13 (
    .a({7{1'b0}}), .b(Instruction[31:25]), .eq(comparator_13_eq));  // open: gt, lt
  Comparator #(.mode("unsigned"), .width(7)) comparator_14 (
    .a(7'b0000001), .b(Instruction[31:25]), .eq(comparator_14_eq));  // open: gt, lt
  Comparator #(.mode("unsigned"), .width(7)) comparator_15 (
    .a(7'b0100000), .b(Instruction[31:25]), .eq(comparator_15_eq));  // open: gt, lt
  Comparator #(.mode("unsigned"), .width(3)) comparator_16 (
    .a(3'b000), .b(Instruction[14:12]), .eq(comparator_16_eq));  // open: gt, lt
  Comparator #(.mode("unsigned"), .width(3)) comparator_17 (
    .a(3'b001), .b(Instruction[14:12]), .eq(comparator_17_eq));  // open: gt, lt
  Comparator #(.mode("unsigned"), .width(3)) comparator_18 (
    .a(3'b010), .b(Instruction[14:12]), .eq(comparator_18_eq));  // open: gt, lt
  Comparator #(.mode("unsigned"), .width(3)) comparator_19 (
    .a(3'b100), .b(Instruction[14:12]), .eq(comparator_19_eq));  // open: gt, lt
  Comparator #(.mode("unsigned"), .width(3)) comparator_20 (
    .a(3'b101), .b(Instruction[14:12]), .eq(comparator_20_eq));  // open: gt, lt
  Comparator #(.mode("unsigned"), .width(3)) comparator_21 (
    .a(3'b110), .b(Instruction[14:12]), .eq(comparator_21_eq));  // open: gt, lt
  Comparator #(.mode("unsigned"), .width(3)) comparator_22 (
    .a(3'b111), .b(Instruction[14:12]), .eq(comparator_22_eq));  // open: gt, lt
  Comparator #(.mode("unsigned"), .width(7)) comparator_23 (
    .a({7{1'b0}}), .b(Instruction[31:25]), .eq(comparator_23_eq));  // open: gt, lt
  Comparator #(.mode("unsigned"), .width(7)) comparator_24 (
    .a(7'b0100000), .b(Instruction[31:25]), .eq(comparator_24_eq));  // open: gt, lt
  and and_1 (and_1_out, comparator_17_eq, comparator_23_eq);
  and and_2 (and_2_out, comparator_20_eq, comparator_23_eq);
  and and_3 (and_3_out, comparator_20_eq, comparator_24_eq);
  and and_4 (and_4_out, comparator_5_eq, comparator_13_eq);
  and and_5 (and_5_out, comparator_5_eq, comparator_14_eq);
  and and_6 (and_6_out, comparator_5_eq, comparator_15_eq);
  and and_7 (and_7_out, comparator_6_eq, comparator_13_eq);
  and and_8 (and_8_out, comparator_6_eq, comparator_14_eq);
  and and_9 (and_9_out, comparator_8_eq, comparator_14_eq);
  and and_10 (and_10_out, comparator_7_eq, comparator_13_eq);
  and and_11 (and_11_out, comparator_9_eq, comparator_13_eq);
  and and_12 (and_12_out, comparator_10_eq, comparator_13_eq);
  and and_13 (and_13_out, comparator_10_eq, comparator_15_eq);
  and and_14 (and_14_out, comparator_11_eq, comparator_13_eq);
  and and_15 (and_15_out, comparator_12_eq, comparator_13_eq);
  assign bit_extender_2_out = {{3{1'b0}}, Instruction[14:12]};  // Bit_Extender bit_extender_2
  Adder #(.width(6)) adder_2 (.a(bit_extender_2_out), .b(6'b001100), .out(adder_2_out));  // open: cin, cout
  Priority_Encoder priority_encoder_2 (
    .in0(comparator_16_eq), .in1(and_1_out), .in2(comparator_18_eq), .in3(comparator_19_eq), .in4(and_2_out),
    .in5(and_3_out), .in6(comparator_21_eq), .in7(comparator_22_eq), .out(priority_encoder_2_out));  // open: en_in, gs, en_out
  Multiplexer #(.width(6)) multiplexer_2 (.in0({6{1'b0}}), .in1(adder_2_out), .out(ROMInputI1), .sel(comparator_25_eq));
  Comparator #(.mode("unsigned"), .width(7)) comparator_25 (
    .a(Instruction[6:0]), .b(7'b0000011), .eq(comparator_25_eq));  // open: gt, lt
  assign bit_extender_3_out = {{3{1'b0}}, priority_encoder_2_out};  // Bit_Extender bit_extender_3
  Priority_Encoder #(.select_enc(4)) priority_encoder_3 (
    .in0(and_4_out), .in1(and_5_out), .in2(and_6_out), .in3(and_7_out), .in4(and_8_out), .in5(and_9_out),
    .in6(and_10_out), .in7(and_11_out), .in8(and_12_out), .in9(and_13_out), .in10(and_14_out),
    .in11(and_15_out), .out(priority_encoder_3_out));  // open: in12, in13, in14, in15, gs, en_out, en_in
  Adder #(.width(6)) adder_3 (.a(bit_extender_3_out), .b(6'b001111), .out(adder_3_out));  // open: cin, cout
  assign bit_extender_4_out = {{2{1'b0}}, priority_encoder_3_out};  // Bit_Extender bit_extender_4
  Multiplexer #(.width(6)) multiplexer_3 (.in0({6{1'b0}}), .in1(adder_3_out), .out(ROMInputI2), .sel(comparator_26_eq));
  Comparator #(.mode("unsigned"), .width(7)) comparator_26 (
    .a(Instruction[6:0]), .b(7'b0010011), .eq(comparator_26_eq));  // open: gt, lt
  Multiplexer #(.width(6)) multiplexer_4 (
    .in0({6{1'b0}}), .in1(bit_extender_4_out), .out(ROMInputR), .sel(comparator_27_eq));
  Comparator #(.mode("unsigned"), .width(7)) comparator_27 (
    .a(Instruction[6:0]), .b(7'b0110011), .eq(comparator_27_eq));  // open: gt, lt
  Comparator #(.mode("unsigned"), .width(3)) comparator_28 (
    .a(3'b000), .b(Instruction[14:12]), .eq(comparator_28_eq));  // open: gt, lt
  Comparator #(.mode("unsigned"), .width(3)) comparator_29 (
    .a(3'b001), .b(Instruction[14:12]), .eq(comparator_29_eq));  // open: gt, lt
  Comparator #(.mode("unsigned"), .width(3)) comparator_30 (
    .a(3'b010), .b(Instruction[14:12]), .eq(comparator_30_eq));  // open: gt, lt
  Comparator #(.mode("unsigned"), .width(3)) comparator_31 (
    .a(3'b000), .b(Instruction[14:12]), .eq(comparator_31_eq));  // open: gt, lt
  Comparator #(.mode("unsigned"), .width(3)) comparator_32 (
    .a(3'b001), .b(Instruction[14:12]), .eq(comparator_32_eq));  // open: gt, lt
  Comparator #(.mode("unsigned"), .width(3)) comparator_33 (
    .a(3'b100), .b(Instruction[14:12]), .eq(comparator_33_eq));  // open: gt, lt
  Comparator #(.mode("unsigned"), .width(3)) comparator_34 (
    .a(3'b101), .b(Instruction[14:12]), .eq(comparator_34_eq));  // open: gt, lt
  Comparator #(.mode("unsigned"), .width(3)) comparator_35 (
    .a(3'b110), .b(Instruction[14:12]), .eq(comparator_35_eq));  // open: gt, lt
  Comparator #(.mode("unsigned"), .width(3)) comparator_36 (
    .a(3'b111), .b(Instruction[14:12]), .eq(comparator_36_eq));  // open: gt, lt
  not not_1 (not_1_out, BrEq);
  not not_2 (not_2_out, BrLt);
  not not_3 (not_3_out, BrLt);
  assign bit_extender_5_out = {{4{1'b0}}, priority_encoder_4_out};  // Bit_Extender bit_extender_5
  Priority_Encoder #(.select_enc(2)) priority_encoder_4 (
    .in0(comparator_28_eq), .in1(comparator_29_eq), .in2(comparator_30_eq), .out(priority_encoder_4_out));  // open: in3, gs, en_out, en_in
  Priority_Encoder priority_encoder_5 (
    .in0(comparator_31_eq), .in1(comparator_32_eq), .in2(comparator_33_eq), .in3(comparator_34_eq),
    .in4(comparator_35_eq), .in5(comparator_36_eq), .out(priority_encoder_5_out));  // open: in6, in7, en_in, gs, en_out
  and and_16 (and_16_out, comparator_31_eq, BrEq);
  and and_17 (and_17_out, comparator_32_eq, not_1_out);
  and and_18 (and_18_out, comparator_33_eq, BrLt);
  and and_19 (and_19_out, comparator_34_eq, not_2_out);
  and and_20 (and_20_out, comparator_35_eq, BrLt);
  and and_21 (and_21_out, comparator_36_eq, not_3_out);
  Adder #(.width(6)) adder_4 (.a(bit_extender_5_out), .b(6'b010111), .out(adder_4_out));  // open: cin, cout
  assign bit_extender_6_out = {{3{1'b0}}, priority_encoder_5_out};  // Bit_Extender bit_extender_6
  Multiplexer #(.width(6)) multiplexer_5 (.in0({6{1'b0}}), .in1(adder_4_out), .out(ROMInputS), .sel(comparator_37_eq));
  Comparator #(.mode("unsigned"), .width(7)) comparator_37 (
    .a(Instruction[6:0]), .b(7'b0100011), .eq(comparator_37_eq));  // open: gt, lt
  Adder #(.width(6)) adder_5 (.a(bit_extender_6_out), .b(6'b011010), .out(adder_5_out));  // open: cin, cout
  Multiplexer #(.width(6)) multiplexer_6 (.in0({6{1'b0}}), .in1(adder_5_out), .out(ROMInputB), .sel(comparator_38_eq));
  Comparator #(.mode("unsigned"), .width(7)) comparator_38 (
    .a(Instruction[6:0]), .b(7'b1100011), .eq(comparator_38_eq));  // open: gt, lt
  or or_5 (or_5_out, and_16_out, and_17_out, and_18_out, and_19_out, and_20_out, and_21_out);
  and and_22 (PCSel1, comparator_38_eq, or_5_out);

  // Other names for the same wires on the sheet: Opcode[6:0] = Instruction[6:0]; Funct3[2:0] = Instruction[14:12];
  //   Funct7[6:0] = Instruction[31:25]

  // Notes on the sheet:
  //   INPUTS to your circuit
  //   Connect ROM Input here ->
  //   contents of rom_1 (hex, n*v repeats v):
  //   1003 1403 1603 1083 1483 1583 1103 1203 1283 1683 1303 1383 41 41 41 1041 10c1 1141 1241 12c1 16c1
  //   1341 13c1 1842 1842 1842 4*64 74 74 1067 17c7 2069 2041
  //   ROM FOR CONTROL LOGIC
  //   DON'T CHANGE THE LOCATIONS OF THE INPUTS AND OUTPUTS!
  //   This is only if you choose to do the ROM option
  //   CONNECT
  //   WIRE
  //   TO
  //   USE
  //   ROM
  //   OUTPUT from your circuit
  //   Reminder: If using ROM, use combinational logic for PCSel
endmodule
