// Logisim project partial-load.circ as structural Verilog: 1 circuit, main circuit partial_load
module partial_load (
  input  [31:0] Instruction,
  input  [31:0] MemAddress,
  input  [31:0] DataFromMem,
  output [31:0] DataToReg
);

  wire and_1_out, and_2_out, and_3_out, and_4_out, and_5_out, and_6_out, and_7_out, and_8_out,
       comparator_1_eq, comparator_2_eq, comparator_3_eq, comparator_4_eq, comparator_5_eq, comparator_6_eq,
       comparator_7_eq;
  wire [2:0] priority_encoder_1_out;
  wire [31:0] DataFromMem0to7, DataFromMem0to15, DataFromMem8to15, DataFromMem8to23, DataFromMem16to23,
       DataFromMem16to31, DataFromMem24to31;

  assign DataFromMem0to7 = {{24{DataFromMem[7]}}, DataFromMem[7:0]};  // Bit_Extender bit_extender_1
  assign DataFromMem8to15 = {{24{DataFromMem[15]}}, DataFromMem[15:8]};  // Bit_Extender bit_extender_2
  assign DataFromMem16to23 = {{24{DataFromMem[23]}}, DataFromMem[23:16]};  // Bit_Extender bit_extender_3
  assign DataFromMem24to31 = {{24{DataFromMem[31]}}, DataFromMem[31:24]};  // Bit_Extender bit_extender_4
  assign DataFromMem0to15 = {{16{DataFromMem[15]}}, DataFromMem[15:0]};  // Bit_Extender bit_extender_5
  assign DataFromMem8to23 = {{16{DataFromMem[23]}}, DataFromMem[23:8]};  // Bit_Extender bit_extender_6
  assign DataFromMem16to31 = {{16{DataFromMem[31]}}, DataFromMem[31:16]};  // Bit_Extender bit_extender_7
  Comparator #(.mode("unsigned"), .width(3)) comparator_1 (
    .a(3'b000), .b(Instruction[14:12]), .eq(comparator_1_eq));  // open: gt, lt
  Comparator #(.mode("unsigned"), .width(3)) comparator_2 (
    .a(3'b001), .b(Instruction[14:12]), .eq(comparator_2_eq));  // open: gt, lt
  Comparator #(.mode("unsigned"), .width(3)) comparator_3 (
    .a(3'b010), .b(Instruction[14:12]), .eq(comparator_3_eq));  // open: gt, lt
  Comparator #(.mode("unsigned"), .width(2)) comparator_4 (
    .a(2'b00), .b(MemAddress[1:0]), .eq(comparator_4_eq));  // open: gt, lt
  Comparator #(.mode("unsigned"), .width(2)) comparator_5 (
    .a(2'b01), .b(MemAddress[1:0]), .eq(comparator_5_eq));  // open: gt, lt
  Comparator #(.mode("unsigned"), .width(2)) comparator_6 (
    .a(2'b10), .b(MemAddress[1:0]), .eq(comparator_6_eq));  // open: gt, lt
  Comparator #(.mode("unsigned"), .width(2)) comparator_7 (
    .a(2'b11), .b(MemAddress[1:0]), .eq(comparator_7_eq));  // open: gt, lt
  and and_1 (and_1_out, comparator_1_eq, comparator_4_eq);
  and and_2 (and_2_out, comparator_1_eq, comparator_5_eq);
  and and_3 (and_3_out, comparator_1_eq, comparator_6_eq);
  and and_4 (and_4_out, comparator_1_eq, comparator_7_eq);
  and and_5 (and_5_out, comparator_2_eq, comparator_4_eq);
  and and_6 (and_6_out, comparator_2_eq, comparator_5_eq);
  and and_7 (and_7_out, comparator_2_eq, comparator_6_eq);
  and and_8 (and_8_out, comparator_3_eq, comparator_4_eq);
  Priority_Encoder priority_encoder_1 (
    .in0(and_1_out), .in1(and_2_out), .in2(and_3_out), .in3(and_4_out), .in4(and_5_out), .in5(and_6_out),
    .in6(and_7_out), .in7(and_8_out), .out(priority_encoder_1_out));  // open: en_in, gs, en_out
  Multiplexer #(.select(3), .width(32)) multiplexer_1 (
    .in0(DataFromMem0to7), .in1(DataFromMem8to15), .in2(DataFromMem16to23), .in3(DataFromMem24to31),
    .in4(DataFromMem0to15), .in5(DataFromMem8to23), .in6(DataFromMem16to31), .in7(DataFromMem),
    .out(DataToReg), .sel(priority_encoder_1_out));

  // Other names for the same wires on the sheet: Funct3[2:0] = Instruction[14:12]; Offset[1:0] = MemAddress[1:0]

  // Notes on the sheet:
  //   INPUTS to your circuit
  //   DON'T CHANGE THE LOCATIONS OF THE INPUTS AND OUTPUTS!
  //   OUTPUT from your circuit
endmodule
