// Logisim project partial-store.circ as structural Verilog: 1 circuit, main circuit partial_store
module partial_store (
  input  [31:0] Instruction,
  input  [31:0] MemAddress,
  input  [31:0] DataFromReg,
  input  MemWEn,
  output [3:0] MemWriteMask,
  output [31:0] DataToMem
);

  wire and_1_out, and_2_out, and_3_out, and_4_out, and_5_out, and_6_out, and_7_out, comparator_1_eq,
       comparator_2_eq, comparator_3_eq, comparator_4_eq, comparator_5_eq, comparator_6_eq, comparator_7_eq,
       comparator_8_eq;
  wire [2:0] priority_encoder_1_out;
  wire [3:0] MemWriteMaskStore;

  Comparator #(.mode("unsigned"), .width(3)) comparator_1 (
    .a(3'b000), .b(Instruction[14:12]), .eq(comparator_1_eq));  // open: gt, lt
  Comparator #(.mode("unsigned"), .width(3)) comparator_2 (
    .a(3'b001), .b(Instruction[14:12]), .eq(comparator_2_eq));  // open: gt, lt
  Comparator #(.mode("unsigned"), .width(3)) comparator_3 (
    .a(3'b010), .b(Instruction[14:12]), .eq(comparator_3_eq));  // open: gt, lt
  Comparator #(.mode("unsigned"), .width(2)) comparator_4 (
    .a(2'b00), .b(MemAddress[1:0]), .eq(comparator_4_eq));  // open: gt, lt
  Comparator #(.mode("unsigned"), .width(2)) comparator_5 (
    .a(2'b01), .b(MemAddress[1:0]), .eq(comparator_5_eq));  // open: gt, lt
  Comparator #(.mode("unsigned"), .width(2)) comparator_6 (
    .a(2'b10), .b(MemAddress[1:0]), .eq(comparator_6_eq));  // open: gt, lt
  Comparator #(.mode("unsigned"), .width(2)) comparator_7 (
    .a(2'b11), .b(MemAddress[1:0]), .eq(comparator_7_eq));  // open: gt, lt
  and and_1 (and_1_out, comparator_1_eq, comparator_4_eq);
  and and_2 (and_2_out, comparator_1_eq, comparator_5_eq);
  and and_3 (and_3_out, comparator_1_eq, comparator_6_eq);
  and and_4 (and_4_out, comparator_1_eq, comparator_7_eq);
  and and_5 (and_5_out, comparator_2_eq, comparator_4_eq);
  and and_6 (and_6_out, comparator_2_eq, comparator_6_eq);
  and and_7 (and_7_out, comparator_3_eq, comparator_4_eq);
  Multiplexer #(.width(4)) multiplexer_1 (
    .in0(4'b0000), .in1(MemWriteMaskStore), .out(MemWriteMask), .sel(comparator_8_eq));
  Comparator #(.mode("unsigned"), .width(7)) comparator_8 (
    .a(7'b0100011), .b(Instruction[6:0]), .eq(comparator_8_eq));  // open: gt, lt
  Priority_Encoder priority_encoder_1 (
    .in0(and_1_out), .in1(and_2_out), .in2(and_3_out), .in3(and_4_out), .in4(and_5_out), .in5(and_6_out),
    .in6(and_7_out), .out(priority_encoder_1_out));  // open: in7, en_in, gs, en_out
  Multiplexer #(.select(3), .width(4)) multiplexer_2 (
    .in0(4'b0001), .in1(4'b0010), .in2(4'b0100), .in3(4'b1000), .in4(4'b0011), .in5(4'b1100), .in6(4'b1111),
    .out(MemWriteMaskStore), .sel(priority_encoder_1_out));  // open: in7
  Multiplexer #(.select(3), .width(32)) multiplexer_3 (
    .in0({{24{1'b0}}, DataFromReg[7:0]}), .in1({{16{1'b0}}, DataFromReg[7:0], {8{1'b0}}}),
    .in2({{8{1'b0}}, DataFromReg[7:0], {16{1'b0}}}), .in3({DataFromReg[7:0], {24{1'b0}}}),
    .in4({{16{1'b0}}, DataFromReg[15:0]}), .in5({DataFromReg[15:0], {16{1'b0}}}), .in6(DataFromReg),
    .out(DataToMem), .sel(priority_encoder_1_out));  // open: in7

  // Other names for the same wires on the sheet: DataFromReg0to7[7:0] = DataFromReg[7:0];
  //   DataFromReg0to15[15:0] = DataFromReg[15:0]; DataFromReg8to15[15:8] = DataFromReg[7:0];
  //   DataFromReg16to23[23:16] = DataFromReg[7:0]; DataFromReg16to31[31:16] = DataFromReg[15:0];
  //   DataFromReg24to31[31:24] = DataFromReg[7:0]; Opcode[6:0] = Instruction[6:0]; Funct3[2:0] = Instruction[14:12];
  //   Offset[1:0] = MemAddress[1:0]

  // Notes on the sheet:
  //   INPUTS to your circuit
  //   DON'T CHANGE THE LOCATIONS OF THE INPUTS AND OUTPUTS!
  //   OUTPUT from your circuit
endmodule
