// Logisim project I-type.circ as structural Verilog: 1 circuit, main circuit run_main
module run_main (
  output [31:0] ra,
  output [31:0] sp,
  output [31:0] t0,
  output [31:0] t1,
  output [31:0] t2,
  output [31:0] s0,
  output [31:0] s1,
  output [31:0] a0,
  output [31:0] RequestedAddress,
  output [31:0] RequestedInstruction,
  output [15:0] TimeStep,
  output halt
);

  wire clk;

  Clock clock_1 (.out(clk));
  // Probe on RequestedAddress
  // cpu_harness cpu_harness_1: pin names not known; wires that end beside it: RequestedInstruction, clk, RequestedAddress, ra, sp, t0, t1, t2, s0, s1, a0
  ROM #(.addrWidth(14), .dataWidth(32)) rom_1 (.addr(RequestedAddress[15:2]), .data(RequestedInstruction));
  // Probe on RequestedInstruction
  Counter #(.max('hffff), .width(16)) counter_1 (.clk(clk), .Q(TimeStep));  // open: clr, load, up, count, D, carry
  Comparator #(.width(16)) comparator_1 (.a(TimeStep), .b(16'h4a), .eq(halt));  // open: gt, lt

  // Other names for the same wires on the sheet: Instruction[31:0] = RequestedInstruction;
  //   ProgramCounter[31:0] = RequestedAddress

  // Notes on the sheet:
  //   contents of rom_1 (hex, n*v repeats v):
  //   100293 2a00293 10000293 7ff00293 fff00293 80000413 f0100313 ff030393 100293 7ff00413 ff00313 1030393
  //   107293 2a07293 10007293 7ff07293 fff07293 80007413 f0107313 ff037393 107293 7ff07413 ff07313 1037393
  //   106293 2a06293 10006293 7ff06293 fff06293 80006413 f0106313 ff036393 106293 7ff06413 ff06313 1036393
  //   106293 2a06293 10006293 7ff06293 fff06293 80006413 f0106313 ff036393 106293 7ff06413 ff06313 1036393
  //   104293 2a04293 10004293 7ff04293 fff04293 80004413 f0104313 ff034393 104293 7ff04413 ff04313 1034393
  //   101293 400293 729293 105293 8000293 22d293 40105293 8000293 4022d293 102293 400293 729293
  //   Instruction Memory
  //   Halts Execution After Constant # of Clock Cycles
  //   Constant
endmodule
